# Fritzing sketch esquematicoProjeto (saved by Fritzing 0.9.2b)
breadboards: 1

parts:
  U1 = NodeMCU V1.0
  C1 = Electrolytic Capacitor [capacitance=1000μF package="1010 [SMD, electrolytic]"]  # not connected
  Nokia_5110_LCD_Module1 = Nokia 5110 LCD basado en PCD8544
  R1 = Resistor [tolerance=±5% resistance=10k package="1206 [SMD]"]
  R5 = Resistor [tolerance=±5% resistance=10k package="1206 [SMD]"]
  R6 = Resistor [tolerance=±5% resistance=220 package="1206 [SMD]"]
  J1 = Screw terminal - 2 pins [package=THT]

nets:
  N1: U1.D2, Nokia_5110_LCD_Module1.RST
  3V3: U1.3V3, Nokia_5110_LCD_Module1.VCC, R1.Pin_0
  GND: U1.GND, Nokia_5110_LCD_Module1.GND, Nokia_5110_LCD_Module1.LIGHT, R5.Pin_1
  N2: U1.D5, Nokia_5110_LCD_Module1.CE
  N3: U1.D6, Nokia_5110_LCD_Module1.DC
  N4: U1.D7, Nokia_5110_LCD_Module1.DIN
  N5: U1.D8, Nokia_5110_LCD_Module1.CLK
  N6: U1.A0, R6.Pin_1, J1.pin2
  N7: R1.Pin_1, R5.Pin_0, R6.Pin_0, J1.pin1

notes:
  Sensor de corrente AC

custom parts:
  NodeMCU V1.0: ESP8266 based NodeMCU
  Nokia 5110 LCD basado en PCD8544: Módulo Nokia 5110 LCD basado en el controlador PCD8544. Versión de 8 pines (sólo entrada).
