# Fritzing sketch projeto-do-mes (saved by Fritzing 0.9.2b)
breadboards: 1

parts:
  Componente1 = Arduino Uno (Rev3)
  T1 = LM35 Temperature Sensor [package="TO92 [THT]"]
  M1 = DC Motor
  R1 = Resistor [tolerance=±5% resistance=220 package="0805 [SMD]"]
  D1 = Rectifier Diode [package="Melf DO-213 AA [SMD]"]
  VCC1 = Battery block 9V
  Q1 = npn-Powertransistor [package="TO220 [THT]"]

nets:
  N1: Componente1.A0, T1.Vout
  N2: Componente1.D3_PWM, R1.Pin_0
  N3: Componente1.5V, T1.+Vs
  GND: Componente1.GND, T1.GND, D1.anode, VCC1.-, Q1.emitter
  N4: M1.pin_1, VCC1.+
  N5: M1.pin_2, D1.cathode, Q1.collector
  N6: R1.Pin_1, Q1.base
