# Fritzing sketch esquematico (saved by Fritzing 0.9.2b)
breadboards: 1

parts:
  U1 = NodeMCU V1.0
  J1 = Power Jack [package=power_jack_pth]
  U2 = 2-Channel 5v Relay Shield [package=relay-2ch5v10a]
  JP1 = Header 2 [package=screwterminal-3.5mm-2_lock]
  JP2 = Header 2 [package=screwterminal-3.5mm-2_lock]

nets:
  N1: U1.D4, U2.IN1
  GND: U1.GND, J1.GND, U2.GND
  N2: U1.D5, U2.IN2
  VIN: U1.Vin, J1.PWR, U2.VCC
  N3: U2.K1-On, JP1.1
  N4: U2.K2-On, JP2.1

notes:
  127/220Vac
  Fonte externa 5VDC
  Carga AC - 01
  Carga AC - 02

custom parts:
  NodeMCU V1.0: ESP8266 based NodeMCU
  2-Channel 5v Relay Shield: 2 Channel 5v Relay Shield w. 2x SPD-06VDC-SD-C
