# Fritzing sketch esquema (saved by Fritzing 0.9.3b)
breadboards: 1

parts:
  Componente1 = Arduino Uno (Rev3)
  Componente2 = Bluetooth HC-05 Macho
  T1 = LM35 Temperature Sensor [package="TO92 [THT]"]
  R1 = Photocell (LDR) [package=THT]
  R2 = Resistor [tolerance=±5% resistance=10k package=THT]
  R3 = Resistor [tolerance=±5% resistance=680 package=THT]
  R4 = Resistor [tolerance=±5% resistance=470 package=THT]

nets:
  N1: Componente1.A0, T1.Vout
  N2: Componente1.A1, R1.pin_0, R2.Pin_1
  N3: Componente1.D2, Componente2.TXD
  N4: Componente1.D3_PWM, R4.Pin_0
  5V: Componente1.5V, Componente2.VCC, T1.+Vs, R2.Pin_0
  GND: Componente1.GND, Componente2.GND, T1.GND, R1.pin_1, R3.Pin_1
  N5: Componente2.RXD, R3.Pin_0, R4.Pin_1
