# Fritzing sketch esquematico (saved by Fritzing 0.9.2b)
breadboards: 1

parts:
  U1 = NodeMCU V1.0
  R1 = Photocell (LDR) [package=THT]
  R2 = Resistor [tolerance=±5% resistance=220 package="2010 [SMD]"]
  LED1 = smd LED [color="Red (633nm)" package="0603 [SMD]"]
  R3 = Resistor [tolerance=±5% resistance=220 package="2010 [SMD]"]

nets:
  N1: U1.D4, R3.Pin_0
  N2: U1.3V3, R1.pin_1
  N3: U1.GND, R2.Pin_0, LED1.cathode
  N4: U1.A0, R1.pin_0, R2.Pin_1
  N5: LED1.anode, R3.Pin_1

custom parts:
  NodeMCU V1.0: ESP8266 based NodeMCU
