# Fritzing sketch pushbuttoneled (saved by Fritzing 0.9.2b)
breadboards: 1

parts:
  R2 = Resistor [tolerance=±5% resistance=220 package="2010 [SMD]"]
  Componente1 = Arduino Uno (Rev3)
  S1 = Momentary Switch [package=ksa_sealed_tac_switch]
  R3 = Resistor [tolerance=±5% resistance=220 package="2010 [SMD]"]
  LED1 = LED - 5mm [color="Red (633nm)" package="5 mm [THT]"]

nets:
  N1: R2.Pin_0, Componente1.GND, LED1.cathode
  N2: R2.Pin_1, S1.4
  N3: Componente1.D8, R3.Pin_0
  N4: Componente1.D2, S1.3
  N5: Componente1.5V, S1.2
  N6: R3.Pin_1, LED1.anode
